// Logisim project Processor.circ as structural Verilog: 8 circuits, main circuit main
module main (
);

  wire button_1_out, clock_1_out, clock_2_out, clock_3_out, clock_4_out, Enable_enabler,
       Reg_Writer_write_enable, ZF;
  wire [3:0] fetch_instr_mem_1_icode, fetch_instr_mem_1_ifun, fetch_instr_mem_1_ra, fetch_instr_mem_1_rb,
       icode, ifun, rA_q, rB_q, Reg_Writer_register;
  wire [7:0] alu_1_out_6, fetch_instr_mem_1_valc, fetch_instr_mem_1_valp, multiplexer_1_out,
       Reg_Writer_write_data, register_1_q, register_file_1_out_8, register_file_1_out_9, val_A_q, val_B_q,
       val_C, val_E_q, val_M, val_P, write_back_1_out_6;

  Register #(.width(4)) u_icode (.D(fetch_instr_mem_1_icode), .Q(icode), .clk(clock_1_out));  // open: en, clr
  Register #(.width(4)) u_ifun (.D(fetch_instr_mem_1_ifun), .Q(ifun), .clk(clock_1_out));  // open: en, clr
  Fetch___Instr_Mem fetch_instr_mem_1 (
    .in_1(multiplexer_1_out), .icode(fetch_instr_mem_1_icode), .ifun(fetch_instr_mem_1_ifun),
    .rA(fetch_instr_mem_1_ra), .rB(fetch_instr_mem_1_rb), .valC(fetch_instr_mem_1_valc),
    .valP(fetch_instr_mem_1_valp));
  Register #(.width(4)) rA (.D(fetch_instr_mem_1_ra), .Q(rA_q), .clk(clock_1_out));  // open: en, clr
  Write_Back write_back_1 (
    .in_1(val_P), .in_2(val_M), ._11_halt(val_C), .icode(icode), .cnd(ZF), .out_6(write_back_1_out_6));
  Register u_val_C (.D(fetch_instr_mem_1_valc), .Q(val_C), .clk(clock_1_out));  // open: en, clr
  Register #(.width(4)) rB (.D(fetch_instr_mem_1_rb), .Q(rB_q), .clk(clock_1_out));  // open: en, clr
  Memory Memory (.Address_Bus(val_E_q), .in_2(val_A_q), .Data_Bus(val_M), .icode(icode));
  Register u_val_P (.D(fetch_instr_mem_1_valp), .Q(val_P), .clk(clock_1_out));  // open: en, clr
  Clock clock_1 (.out(clock_1_out));
  ALU alu_1 (
    .out_7(ZF), .icode(icode), .out_6(alu_1_out_6), .val_C(val_C), .val_A(val_A_q), .val_B(val_B_q),
    .ifun(ifun));
  Multiplexer #(.width(8), .enable("false")) multiplexer_1 (
    .in0(register_1_q), .in1({8{1'b0}}), .out(multiplexer_1_out), .sel(button_1_out));
  Button button_1 (.out(button_1_out));
  Register val_E (.D(alu_1_out_6), .en(icode[3]), .Q(val_E_q), .clk(clock_2_out));  // open: clr
  Clock clock_2 (.out(clock_2_out));
  Val_A_B_enabler Enable (.icode(icode), .enabler(Enable_enabler));
  Register val_A (.D(register_file_1_out_8), .en(Enable_enabler), .Q(val_A_q), .clk(clock_3_out));  // open: clr
  Register_File register_file_1 (
    .in_5(Reg_Writer_write_data), .in_6(Reg_Writer_write_enable), .in_7(Reg_Writer_register),
    .out_8(register_file_1_out_8), .in_1(Enable_enabler), .in_2(rA_q), .out_9(register_file_1_out_9),
    .in_3(Enable_enabler), .in_4(rB_q));
  Register val_B (.D(register_file_1_out_9), .en(Enable_enabler), .Q(val_B_q), .clk(clock_3_out));  // open: clr
  Clock clock_3 (.out(clock_3_out));
  Register register_1 (.D(write_back_1_out_6), .Q(register_1_q), .clk(clock_4_out));  // open: en, clr
  Register_Write_Decoder Reg_Writer (
    .val_M(val_M), .val_E(val_E_q), .val_A(val_A_q), .val_C(val_C), .register(Reg_Writer_register),
    .write_data(Reg_Writer_write_data), .icode(icode), .rA(rA_q), .rB(rB_q),
    .write_enable(Reg_Writer_write_enable));
  Clock #(.highDuration(4), .lowDuration(3)) clock_4 (.out(clock_4_out));
endmodule

module ALU (
  input  [3:0] ifun,
  input  [7:0] val_B,
  input  [7:0] val_C,
  input  [7:0] val_A,
  input  [3:0] icode,
  output [7:0] out_6,
  output out_7
);

  wire add_out, clock_1_out, ld_out, mul_out, nor_1_out, not_1_out, not_2_out, not_3_out, not_4_out,
       not_5_out, not_6_out, or_1_out, st_out, val_A_out;
  wire [7:0] adder_1_out, multiplexer_2_out, multiplier_1_out;

  and ld (ld_out, icode[3], icode[2], not_1_out, icode[0]);
  not not_1 (not_1_out, icode[1]);
  and st (st_out, icode[3], icode[2], icode[1], not_2_out);
  not not_2 (not_2_out, icode[0]);
  and add (add_out, icode[3], icode[2], icode[1], icode[0]);
  not not_3 (not_3_out, icode[2]);
  and mul (mul_out, icode[3], not_3_out, not_4_out, not_5_out);
  not not_4 (not_4_out, icode[1]);
  not not_5 (not_5_out, icode[0]);
  nor nor_1 (nor_1_out, out_6[0], out_6[1], out_6[2], out_6[3], out_6[4], out_6[5], out_6[6], out_6[7]);
  Register #(.width(1)) ZF (.D(nor_1_out), .en(ifun[1]), .Q(out_7), .clk(clock_1_out));  // open: clr
  Clock clock_1 (.out(clock_1_out));
  or u_val_A (val_A_out, add_out, mul_out);
  or or_1 (or_1_out, ld_out, st_out, add_out, mul_out);
  Multiplexer #(.width(8), .disabled(0), .enable("false")) multiplexer_1 (
    .in0(adder_1_out), .in1(multiplier_1_out), .out(out_6), .sel(not_6_out));
  not not_6 (not_6_out, ifun[0]);
  Adder adder_1 (.a(multiplexer_2_out), .b(val_B), .out(adder_1_out));  // open: cin, cout
  Multiplexer #(.width(8), .disabled(0)) multiplexer_2 (
    .in0(val_C), .in1(val_A), .out(multiplexer_2_out), .sel(val_A_out), .en(or_1_out));
  Multiplier multiplier_1 (.a(multiplexer_2_out), .b(val_B), .out(multiplier_1_out));  // open: cin, cout

  // Notes on the sheet:
  //   bit 0(right): 1 = add, 0 = multiply
  //   bit 1: 0 = don't update ZF, 1 = update ZF
endmodule

// Reg File
module Register_File (
  input  in_1,
  input  [3:0] in_2,
  input  in_3,
  input  [3:0] in_4,
  input  [7:0] in_5,
  input  in_6,
  input  [3:0] in_7,
  output [7:0] out_8,
  output [7:0] out_9
);

  wire clock_1_out;
  wire [7:0] A_q, B_q, C_q, D_q, demultiplexer_2_out0, demultiplexer_2_out1, demultiplexer_2_out2,
       demultiplexer_2_out3, demultiplexer_2_out4, demultiplexer_2_out5, demultiplexer_2_out6,
       demultiplexer_2_out7, demultiplexer_2_out8, demultiplexer_2_out9, demultiplexer_2_out10,
       demultiplexer_2_out11, demultiplexer_2_out12, demultiplexer_2_out13, demultiplexer_2_out14,
       demultiplexer_2_out15, E_q, F_q, G_q, H_q, I_q, J_q, K_q, L_q, M_q, N_q, rbp_q, rsp_q;
  wire [15:0] demultiplexer_1_out0;

  Demultiplexer #(.select(4), .enable("false")) demultiplexer_1 (
    .out0(demultiplexer_1_out0[0]), .out1(demultiplexer_1_out0[1]), .out2(demultiplexer_1_out0[2]),
    .out3(demultiplexer_1_out0[3]), .out4(demultiplexer_1_out0[4]), .out5(demultiplexer_1_out0[5]),
    .out6(demultiplexer_1_out0[6]), .out7(demultiplexer_1_out0[7]), .out8(demultiplexer_1_out0[8]),
    .out9(demultiplexer_1_out0[9]), .out10(demultiplexer_1_out0[10]), .out11(demultiplexer_1_out0[11]),
    .out12(demultiplexer_1_out0[12]), .out13(demultiplexer_1_out0[13]), .out14(demultiplexer_1_out0[14]),
    .out15(demultiplexer_1_out0[15]), .in(in_6), .sel(in_7));
  Demultiplexer #(.select(4), .width(8), .disabled(0)) demultiplexer_2 (
    .out0(demultiplexer_2_out0), .out1(demultiplexer_2_out1), .out2(demultiplexer_2_out2),
    .out3(demultiplexer_2_out3), .out4(demultiplexer_2_out4), .out5(demultiplexer_2_out5),
    .out6(demultiplexer_2_out6), .out7(demultiplexer_2_out7), .out8(demultiplexer_2_out8),
    .out9(demultiplexer_2_out9), .out10(demultiplexer_2_out10), .out11(demultiplexer_2_out11),
    .out12(demultiplexer_2_out12), .out13(demultiplexer_2_out13), .out14(demultiplexer_2_out14),
    .out15(demultiplexer_2_out15), .in(in_5), .sel(in_7), .en(in_6));
  Clock clock_1 (.out(clock_1_out));
  Register A (.D(demultiplexer_2_out0), .en(demultiplexer_1_out0[0]), .Q(A_q), .clk(clock_1_out));  // open: clr
  Register B (.D(demultiplexer_2_out1), .en(demultiplexer_1_out0[1]), .Q(B_q), .clk(clock_1_out));  // open: clr
  Register C (.D(demultiplexer_2_out2), .en(demultiplexer_1_out0[2]), .Q(C_q), .clk(clock_1_out));  // open: clr
  Register D (.D(demultiplexer_2_out3), .en(demultiplexer_1_out0[3]), .Q(D_q), .clk(clock_1_out));  // open: clr
  Register E (.D(demultiplexer_2_out4), .en(demultiplexer_1_out0[4]), .Q(E_q), .clk(clock_1_out));  // open: clr
  Register F (.D(demultiplexer_2_out5), .en(demultiplexer_1_out0[5]), .Q(F_q), .clk(clock_1_out));  // open: clr
  Register G (.D(demultiplexer_2_out6), .en(demultiplexer_1_out0[6]), .Q(G_q), .clk(clock_1_out));  // open: clr
  Register H (.D(demultiplexer_2_out7), .en(demultiplexer_1_out0[7]), .Q(H_q), .clk(clock_1_out));  // open: clr
  Register I (.D(demultiplexer_2_out8), .en(demultiplexer_1_out0[8]), .Q(I_q), .clk(clock_1_out));  // open: clr
  Register J (.D(demultiplexer_2_out9), .en(demultiplexer_1_out0[9]), .Q(J_q), .clk(clock_1_out));  // open: clr
  Register K (.D(demultiplexer_2_out10), .en(demultiplexer_1_out0[10]), .Q(K_q), .clk(clock_1_out));  // open: clr
  Register L (.D(demultiplexer_2_out11), .en(demultiplexer_1_out0[11]), .Q(L_q), .clk(clock_1_out));  // open: clr
  Register M (.D(demultiplexer_2_out12), .en(demultiplexer_1_out0[12]), .Q(M_q), .clk(clock_1_out));  // open: clr
  Register N (.D(demultiplexer_2_out13), .en(demultiplexer_1_out0[13]), .Q(N_q), .clk(clock_1_out));  // open: clr
  Register rbp (.D(demultiplexer_2_out14), .en(demultiplexer_1_out0[14]), .Q(rbp_q), .clk(clock_1_out));  // open: clr
  Register rsp (.D(demultiplexer_2_out15), .en(demultiplexer_1_out0[15]), .Q(rsp_q), .clk(clock_1_out));  // open: clr
  Multiplexer #(.select(4), .width(8), .disabled(0)) multiplexer_1 (
    .in0(A_q), .in1(B_q), .in2(C_q), .in3(D_q), .in4(E_q), .in5(F_q), .in6(G_q), .in7(H_q), .in8(I_q),
    .in9(J_q), .in10(K_q), .in11(L_q), .in12(M_q), .in13(N_q), .in14(rbp_q), .in15(rsp_q), .out(out_8),
    .sel(in_2), .en(in_1));
  Multiplexer #(.select(4), .width(8), .disabled(0)) multiplexer_2 (
    .in0(A_q), .in1(B_q), .in2(C_q), .in3(D_q), .in4(E_q), .in5(F_q), .in6(G_q), .in7(H_q), .in8(I_q),
    .in9(J_q), .in10(K_q), .in11(L_q), .in12(M_q), .in13(N_q), .in14(rbp_q), .in15(rsp_q), .out(out_9),
    .sel(in_4), .en(in_3));
endmodule

module Memory (
  input  [7:0] Address_Bus,
  input  [7:0] in_2,
  input  [3:0] icode,
  output [7:0] Data_Bus
);

  wire clock_1_out, not_1_out, not_2_out, or_1_out, read_out, write_out;
  wire [7:0] ram_1_data, register_1_q;

  not not_1 (not_1_out, icode[1]);
  not not_2 (not_2_out, icode[0]);
  Register register_1 (.D(Address_Bus), .Q(register_1_q), .clk(clock_1_out));  // open: en, clr
  and read (read_out, icode[3], icode[2], not_1_out, icode[0]);
  and write (write_out, icode[3], icode[2], icode[1], not_2_out);
  Clock clock_1 (.out(clock_1_out));
  or or_1 (or_1_out, write_out, read_out);
  RAM #(.bus("separate")) ram_1 (
    .addr(register_1_q), .din(in_2), .data(ram_1_data), .str(write_out), .sel(or_1_out), .clk(clock_1_out),
    .ld(read_out));  // open: clr
  Register register_2 (.D(ram_1_data), .Q(Data_Bus), .clk(clock_1_out));  // open: en, clr

  // Notes on the sheet:
  //   00 - Do Nothing
  //   01 - Read
  //   10 - Write
  //   Data_in
  //   RAM
  //   ROM
endmodule

module Write_Back (
  input  [7:0] in_1,
  input  [7:0] in_2,
  input  [7:0] _11_halt,
  input  [3:0] icode,
  input  cnd,
  output [7:0] out_6
);

  wire jmp_out, jz_T_out, not_1_out, not_2_out, not_3_out, not_4_out, not_5_out, not_6_out, not_7_out,
       not_8_out, not_9_out, not_10_out, not_11_out, not_12_out;
  wire [1:0] halt_out;

  not not_1 (not_1_out, icode[3]);
  and jmp (jmp_out, not_1_out, icode[2], icode[1], icode[0]);
  and jz_T (jz_T_out, not_3_out, not_4_out, not_2_out, icode[0], cnd);
  not not_2 (not_2_out, icode[1]);
  not not_3 (not_3_out, icode[3]);
  not not_4 (not_4_out, icode[2]);
  Multiplexer #(.select(2), .width(8)) multiplexer_1 (
    .in0(in_1), .in1(in_2), .in2(_11_halt), .in3({8{1'b1}}), .out(out_6), .sel(halt_out));  // open: en
  or or_1 (halt_out[1], jmp_out, jz_T_out, halt_out[0]);
  // AND_Gate jz_F has open pins: in0=not_5_out, in1=not_10_out, in2=not_8_out, in3=icode[0], in4=not_6_out, out=open
  not not_5 (not_5_out, icode[3]);
  not not_6 (not_6_out, cnd);
  not not_7 (not_7_out, icode[2]);
  not not_8 (not_8_out, icode[1]);
  not not_9 (not_9_out, icode[3]);
  not not_10 (not_10_out, icode[2]);
  and halt (halt_out[0], not_9_out, not_7_out, not_12_out, not_11_out);
  not not_11 (not_11_out, icode[0]);
  not not_12 (not_12_out, icode[1]);

  // Notes on the sheet:
  //   INPUTS
  //   00 ValP
  //   01 ValM
  //   10 ValC
  //   icode:
  //   irmov - 11
  //   rrmovl - 100
  //   ld - 1101
  //   st -1110
  //   jmp - 111
  //   jz - 0001
  //   halt - 0
  //   add - 1111
  //   mul - 1000
  //   PC <- valP
  //   PC <- valP
  //   PC <- valP
  //   PC <- valP
  //   PC <-val C
  //   PC <- 11111111
  //   PC <- valP
  //   PC <- valP
  //   PC <- cnd ? val C : val P
endmodule

module Val_A_B_enabler (
  input  [3:0] icode,
  output enabler
);

  wire add_out, ld_out, mul_out, not_1_out, not_2_out, not_3_out, not_4_out, not_5_out, not_6_out, not_7_out,
       not_8_out, rrmov_out, st_out;

  not not_1 (not_1_out, icode[0]);
  not not_2 (not_2_out, icode[1]);
  not not_3 (not_3_out, icode[2]);
  not not_4 (not_4_out, icode[1]);
  not not_5 (not_5_out, icode[0]);
  not not_6 (not_6_out, icode[3]);
  not not_7 (not_7_out, icode[1]);
  not not_8 (not_8_out, icode[0]);
  and st (st_out, icode[3], icode[2], icode[1], not_1_out);
  and ld (ld_out, icode[3], icode[2], not_2_out, icode[0]);
  and add (add_out, icode[3], icode[2], icode[1], icode[0]);
  and mul (mul_out, icode[3], not_3_out, not_4_out, not_5_out);
  and rrmov (rrmov_out, not_6_out, icode[2], not_7_out, not_8_out);
  or or_1 (enabler, st_out, ld_out, add_out, mul_out, rrmov_out);
endmodule

module Register_Write_Decoder (
  input  [3:0] icode,
  input  [3:0] rA,
  input  [3:0] rB,
  input  [7:0] val_M,
  input  [7:0] val_E,
  input  [7:0] val_A,
  input  [7:0] val_C,
  output write_enable,
  output [3:0] register,
  output [7:0] write_data
);

  wire add_out, irmov_out, ld_out, mul_out, not_1_out, not_2_out, not_3_out, not_4_out, not_5_out, not_6_out,
       not_7_out, not_8_out, not_9_out, rrmov_out, write_rB_out;
  wire [1:0] b_c_e_out;

  not not_1 (not_1_out, icode[1]);
  not not_2 (not_2_out, icode[2]);
  not not_3 (not_3_out, icode[1]);
  not not_4 (not_4_out, icode[0]);
  not not_5 (not_5_out, icode[3]);
  not not_6 (not_6_out, icode[1]);
  not not_7 (not_7_out, icode[0]);
  not not_8 (not_8_out, icode[3]);
  not not_9 (not_9_out, icode[2]);
  and ld (ld_out, icode[3], icode[2], not_1_out, icode[0]);
  and add (add_out, icode[3], icode[2], icode[1], icode[0]);
  and mul (mul_out, icode[3], not_2_out, not_3_out, not_4_out);
  and rrmov (rrmov_out, not_5_out, icode[2], not_6_out, not_7_out);
  and irmov (irmov_out, not_8_out, not_9_out, icode[1], icode[0]);
  or b_c_e (b_c_e_out[0], add_out, mul_out, irmov_out);
  or d_e (b_c_e_out[1], rrmov_out, irmov_out);
  Multiplexer #(.select(2), .width(8), .disabled(0)) multiplexer_1 (
    .in0(val_M), .in1(val_E), .in2(val_A), .in3(val_C), .out(write_data), .sel(b_c_e_out), .en(write_enable));
  or write_rB (write_rB_out, add_out, mul_out, rrmov_out);
  Multiplexer #(.width(4), .disabled(0)) multiplexer_2 (
    .in0(rA), .in1(rB), .out(register), .sel(write_rB_out), .en(write_enable));
  or or_1 (write_enable, ld_out, add_out, mul_out, rrmov_out, irmov_out);
endmodule

module Fetch___Instr_Mem (
  input  [7:0] in_1,
  output [3:0] icode,
  output [3:0] ifun,
  output [3:0] rA,
  output [3:0] rB,
  output [7:0] valC,
  output [7:0] valP
);

  wire _0001_out, _0111_out, clock_1_out, nand_1_out, or_1_out;
  wire [7:0] bit_extender_1_out, demultiplexer_1_out1, register_1_q, register_1_q_2;
  wire [23:0] rom_1_data;

  nand nand_1 (nand_1_out, in_1[0], in_1[1], in_1[2], in_1[3], in_1[4], in_1[5], in_1[6], in_1[7]);
  ROM #(.dataWidth(24)) rom_1 (.addr(in_1), .data(rom_1_data), .sel(nand_1_out));
  Clock #(.highDuration(4), .lowDuration(4)) clock_1 (.out(clock_1_out));
  Register #(.width(24)) register_1 (
    .D(rom_1_data), .en(nand_1_out), .Q({icode, ifun, register_1_q_2, register_1_q}), .clk(clock_1_out));  // open: clr
  or or_1 (or_1_out, _0001_out, _0111_out);
  and _0111 (_0111_out, icode[3], icode[2], icode[1], ~icode[0]);  // AND_Gate
  and _0001 (_0001_out, ~icode[3], ~icode[2], ~icode[1], icode[0]);  // AND_Gate
  Demultiplexer #(.width(8), .enable("false")) demultiplexer_1 (
    .out0({rA, rB}), .out1(demultiplexer_1_out1), .in(register_1_q_2), .sel(or_1_out));
  Multiplexer #(.width(8), .enable("false")) multiplexer_1 (
    .in0(register_1_q), .in1(demultiplexer_1_out1), .out(valC), .sel(or_1_out));
  assign bit_extender_1_out = {{7{1'b0}}, 1'b1};  // Bit_Extender bit_extender_1
  Adder adder_1 (.a(bit_extender_1_out), .b(in_1), .out(valP));  // open: cin, cout

  // Notes on the sheet:
  //   PC
  //   INPUTS
  //   Instruction Memory
  //   contents of rom_1 (hex, n*v repeats v):
  //   301004 401500 302040 303050 304060 d15200 d16300 f35600 e15400 f35200 f35300 f35400 305fff f35100
  //   100500
  //   icode
  //   Byte 2
  //   ifun
  //   Byte 3
  //   (ic,0,rA,0,A)
  //   (ic, 0, ra, rb)
  //   (ic, 11, ra, rb)
  //   (ic, 10, ra, rb)
  //   icode:
  //   irmov - 0011
  //   rrmovl - 0100
  //   ld - 1101
  //   (ic, 1, ra, rb, D)
  //   st -1110
  //   (ic, 1, ra, rb, D)
  //   (ic, 0, D)
  //   jmp - 0111
  //   halt - 0000
  //   add - 1111
  //   mul - 1000
  //   call - 0010
  //   (ic, 0, D)
  //   return - 0001
  //   (ic, 0)
  //   valP <- PC + 3
  //   valP <- PC + 2
  //   valP <- PC + 3
  //   valP <- PC + 3
  //   valP <- PC + 2
  //   valP <- PC + 2
  //   valP <- PC + 2
  //   valP <- PC + 2
  //   valP <- PC + 1
  //   valC <- M[PC + 1]
  //   valC <- M[PC + 1]
  //   valC <- M[PC + 1]
endmodule
