// Logisim project ape.circ as structural Verilog: 1 circuit, main circuit main
module main (
  input  [7:0] Address_Bus,
  input  [7:0] in_2,
  input  in_3,
  input  _10___Write,
  input  in_5,
  output [7:0] Data_Bus
);

  wire _01_out, _10_out, clock_1_out, sel_out;
  wire [7:0] ram_1_data, register_1_q;

  Register register_1 (.D(Address_Bus), .Q(register_1_q), .clk(clock_1_out));  // open: en, clr
  and _01 (_01_out, ~_10___Write, in_5);  // AND_Gate
  and _10 (_10_out, _10___Write, ~in_5);  // AND_Gate
  xor sel (sel_out, _10___Write, in_5);
  Clock clock_1 (.out(clock_1_out));
  RAM #(.bus("separate")) ram_1 (
    .addr(register_1_q), .din(in_2), .data(ram_1_data), .str(_01_out), .sel(sel_out), .clk(clock_1_out),
    .ld(_10_out));  // open: clr
  ROM rom_1 (.addr(register_1_q), .data(ram_1_data), .sel(in_3));
  Register register_2 (.D(ram_1_data), .Q(Data_Bus), .clk(clock_1_out));  // open: en, clr

  // Notes on the sheet:
  //   00 - Do Nothing
  //   01 - Read
  //   Data_in
  //   RAM
  //   store_data_en
  //   load_data_en
  //   ROM
  //   contents of rom_1 (hex, n*v repeats v):
  //   f 0 0 0 f
  //   ROM_select_en
endmodule
