// Logisim project writebc.circ as structural Verilog: 1 circuit, main circuit main
module main (
  input  [7:0] in_1,
  input  [7:0] in_2,
  input  [7:0] in_3,
  input  [3:0] icode,
  input  cnd,
  output [7:0] out_6
);

  wire _0001_out, _0010_out, _0011_out, _0100_out, _0111_2_out, _0111_out, _1000_out, _1101_out, _1110_out,
       _1111_out;
  wire [1:0] or_1_out;

  and _0100 (_0100_out, ~icode[0], ~icode[1], icode[2], ~icode[3]);  // AND_Gate
  and _0011 (_0011_out, icode[0], icode[1], ~icode[2], ~icode[3]);  // AND_Gate
  or or_1 (or_1_out[0], _0100_out, _0011_out, _1101_out, _1110_out, _1000_out, _1111_out, _0111_out, _0111_2_out, _0010_out);
  and _1110 (_1110_out, ~icode[0], icode[1], icode[2], icode[3]);  // AND_Gate
  and _1101 (_1101_out, icode[0], ~icode[1], icode[2], icode[3]);  // AND_Gate
  and _1000 (_1000_out, ~icode[0], ~icode[1], ~icode[2]);  // AND_Gate
  and _1111 (_1111_out, icode[0], icode[1], icode[2], icode[3]);
  Multiplexer #(.select(2), .width(8)) multiplexer_1 (
    .in1(in_1), .in2(in_2), .in3(in_3), .out(out_6), .sel(or_1_out));  // open: in0, en
  and _0111 (_0111_out, icode[0], icode[1], ~cnd, icode[2], ~icode[3]);  // AND_Gate
  or or_2 (or_1_out[1], _0111_2_out, _0010_out, _0001_out);
  and _0010 (_0010_out, ~icode[0], icode[1], ~icode[2], ~icode[3]);  // AND_Gate
  and _0111_2 (_0111_2_out, icode[0], icode[1], cnd, icode[2], ~icode[3]);  // AND_Gate
  and _0001 (_0001_out, icode[0], ~icode[1], ~icode[2], ~icode[3]);  // AND_Gate

  // Notes on the sheet:
  //   INPUTS
  //   01 ValP
  //   10 ValM
  //   11 ValC
  //   icode:
  //   irmov - 11
  //   rrmovl - 100
  //   ld - 1101
  //   st -1110
  //   jmp - 111
  //   halt - 0
  //   add - 1111
  //   mul - 1000
  //   call - 10
  //   return - 1
  //   PC <- valP
  //   PC <- valP
  //   PC <- valP
  //   PC <- valP
  //   PC <- valP
  //   PC <- valP
  //   PC <- valC
  //   PC <- valM
  //   PC <- cond ? valC : val P
  //   10 valM = 0001
  //   11 valC = 0010 + 0111*cnd
  //   01 valP = 0011 + 0100 + 1101 + 1110 + 0111*cnd' + 1111 + 1000 
endmodule
